# Fritzing sketch circuit_diagram (saved by Fritzing 0.9.3b)
breadboards: 17
perfboards: 1

parts:
  U1 = IC, DIP package, 20 pins [chip_label=SN74LS682N]
  U2 = IC, DIP package, 20 pins [chip_label=SN74LS682N]
  U3 = IC, DIP package, 20 pins [chip_label=SN74LS244N]
  U4 = IC, DIP package, 20 pins [chip_label=SN74LS244N]
  U5 = IC, DIP package, 14 pins [chip_label=SN74LS74AN]
  U6 = IC, DIP package, 14 pins [chip_label=SN74HCT32N]
  U7 = IC, DIP package, 20 pins [chip_label=SN74LS682N]
  U8 = IC, DIP package, 20 pins [chip_label=SN74LS682N]
  U9 = IC, DIP package, 14 pins [chip_label=SN74HCT32N]
  U10 = IC, DIP package, 20 pins [chip_label=SN74LS245N]
  U11 = IC, DIP package, 20 pins [chip_label=SN74LS682N]
  U12 = IC, DIP package, 20 pins [chip_label=SN74LS682N]
  U13 = IC, DIP package, 20 pins [chip_label=SN74LS682N]
  U14 = IC, DIP package, 20 pins [chip_label=SN74LS682N]
  U15 = IC, DIP package, 20 pins [chip_label=SN74LS245N]
  U16 = IC, DIP package, 20 pins [chip_label=SN74LS244N]
  U17 = IC, DIP package, 14 pins [chip_label=SN74LS74AN]
  U18 = IC, DIP package, 20 pins [chip_label=SN74LS682N]
  U19 = IC, DIP package, 20 pins [chip_label=SN74LS682N]
  U20 = IC, DIP package, 16 pins [chip_label=SN74LS161A]
  U21 = IC, DIP package, 16 pins [chip_label=SN74LS161A]
  U22 = IC, DIP package, 14 pins [chip_label=SN74HCT32N]
  U23 = IC, DIP package, 16 pins [chip_label=SN74LS161A]
  U24 = IC, DIP package, 20 pins [chip_label=SN74LS244N]
  U25 = IC, DIP package, 16 pins [chip_label=SN74LS161A]
  U26 = IC, DIP package, 16 pins [chip_label=SN74LS161A]
  U27 = IC, DIP package, 20 pins [chip_label=SN74LS682N]
  U28 = IC, DIP package, 20 pins [chip_label=SN74LS682N]
  U29 = IC, DIP package, 20 pins [chip_label=SN74LS244N]
  U30 = IC, DIP package, 14 pins [chip_label=SN74HCT32N]
  U31 = IC, DIP package, 14 pins [chip_label=SN74LS74AN]
  U32 = IC, DIP package, 16 pins [chip_label=SN74LS161A]
  U33 = IC, DIP package, 16 pins [chip_label=SN74LS283N]
  U34 = IC, DIP package, 16 pins [chip_label=SN74LS283N]
  U35 = IC, DIP package, 16 pins [chip_label=SN74LS283N]
  U36 = IC, DIP package, 16 pins [chip_label=SN74LS283N]
  U37 = IC, DIP package, 20 pins [chip_label=SN74LS682N]
  U38 = IC, DIP package, 20 pins [chip_label=SN74LS682N]
  U39 = IC, DIP package, 20 pins [chip_label=SN74LS273N]
  U40 = IC, DIP package, 20 pins [chip_label=SN74LS273N]
  U41 = IC, DIP package, 16 pins [chip_label=SN74LS161A]
  U42 = IC, DIP package, 16 pins [chip_label=SN74LS161A]
  U43 = IC, DIP package, 20 pins [chip_label=SN74HCT374N]
  U44 = IC, DIP package, 20 pins [chip_label=SN74HCT374N]
  U45 = IC, DIP package, 14 pins [chip_label=SN74LS74AN]
  U46 = IC, DIP package, 14 pins [chip_label=SN74HCT32N]
  U47 = IC, DIP package, 20 pins [chip_label=SN74LS244N]
  U48 = IC, DIP package, 20 pins [chip_label=SN74LS245N]
  U49 = IC, DIP package, 20 pins [chip_label=SN74LS245N]
  U50 = IC, DIP package, 20 pins [chip_label=SN74LS245N]
  U51 = IC, DIP package, 20 pins [chip_label=SN74LS682N]
  U52 = IC, DIP package, 20 pins [chip_label=SN74LS682N]
  U53 = IC, DIP package, 14 pins [chip_label=SN74LS08N]
  U54 = IC, DIP package, 14 pins [chip_label=SN74LS04N]
  U55 = IC, DIP package, 14 pins [chip_label=SN74LS74AN]
  U56 = IC, DIP package, 28 pins [chip_label=CY7C199-55PC]
  U57 = IC, DIP package, 20 pins [chip_label=SN74LS244N]
  U58 = IC, DIP package, 20 pins [chip_label=SN74LS244N]
  U59 = IC, DIP package, 20 pins [chip_label=SN74LS244N]
  U60 = IC, DIP package, 20 pins [chip_label=SN74LS244N]
  U61 = IC, DIP package, 20 pins [chip_label=SN74LS244N]
  U62 = IC, DIP package, 20 pins [chip_label=SN74LS273N]
  U63 = IC, DIP package, 16 pins [chip_label=SN74LS161A]
  U64 = IC, DIP package, 16 pins [chip_label=SN74LS161A]
  U65 = IC, DIP package, 20 pins [chip_label=SN74LS273N]
  U66 = IC, DIP package, 16 pins [chip_label=SN74LS283N]
  U67 = IC, DIP package, 16 pins [chip_label=SN74LS283N]
  U68 = IC, DIP package, 16 pins [chip_label=SN74LS283N]
  U69 = IC, DIP package, 16 pins [chip_label=SN74LS283N]
  U70 = IC, DIP package, 20 pins [chip_label=SN74LS273N]
  U71 = IC, DIP package, 20 pins [chip_label=SN74LS273N]
  U72 = IC, DIP package, 20 pins [chip_label=SN74LS273N]
  25_175_MHz = CRYSTAL - kHz [frequency="32 kHz"]  # not connected
  U73 = IC, DIP package, 20 pins [chip_label=SN74LS273N]  # not connected
  U74 = IC, DIP package, 20 pins [chip_label=SN74LS273N]  # not connected
  U75 = IC, DIP package, 14 pins [chip_label=SN74LS04N]  # not connected
  U76 = IC, DIP package, 20 pins [chip_label=SN74LS244N]
  U77 = IC, DIP package, 20 pins [chip_label=SN74LS682N]
  U78 = IC, DIP package, 20 pins [chip_label=SN74LS682N]
  U79 = IC, DIP package, 20 pins [chip_label=SN74LS682N]
  U80 = IC, DIP package, 14 pins [chip_label=SN74HCT32N]
  U81 = IC, DIP package, 14 pins [chip_label=SN74HCT32N]
  U82 = IC, DIP package, 14 pins [chip_label=SN74LS04N]
  U83 = IC, DIP package, 20 pins [chip_label=SN74LS682N]

nets:
  N1: U1.pin10, U1.pin20, U2.pin10, U3.pin10, U7.pin10, U8.pin10, U9.pin7, U10.pin10, U11.pin10, U12.pin10, U13.pin10, U14.pin10, U15.pin10, U16.pin10, U17.pin7, U18.pin10, U19.pin10, U20.pin8, U21.pin8, U22.pin7, U23.pin8, U24.pin10, U25.pin8, U26.pin8, U27.pin10, U28.pin10, U29.pin10, U30.pin7, U31.pin7, U32.pin8, U33.pin8, U34.pin8, U35.pin8, U36.pin8, U37.pin10, U38.pin10, U39.pin10, U40.pin10, U41.pin8, U42.pin8, U43.pin10, U44.pin10, U45.pin7, U46.pin7, U47.pin10, U48.pin10, U49.pin10, U50.pin10, U51.pin10, U52.pin10, U53.pin7, U54.pin7, U55.pin7, U56.pin14, U57.pin10, U58.pin10, U59.pin10, U60.pin10, U61.pin10, U62.pin10, U63.pin8, U64.pin8, U65.pin10, U66.pin8, U67.pin8, U68.pin8, U69.pin8, U70.pin10, U71.pin10, U72.pin10, U76.pin10, U77.pin10, U78.pin10, U79.pin10, U80.pin7, U81.pin7, U82.pin7, U83.pin10
  N2: U2.pin20, U3.pin20, U4.pin20, U5.pin14, U6.pin14, U7.pin20, U8.pin20, U9.pin14, U10.pin20, U11.pin20, U12.pin20, U13.pin20, U14.pin20, U15.pin20, U16.pin20, U17.pin14, U18.pin20, U19.pin20, U20.pin16, U21.pin16, U22.pin14, U23.pin16, U24.pin20, U25.pin16, U26.pin16, U27.pin20, U28.pin20, U29.pin20, U30.pin14, U31.pin14, U32.pin16, U33.pin16, U34.pin16, U35.pin16, U36.pin16, U37.pin20, U38.pin20, U39.pin20, U40.pin20, U41.pin16, U42.pin16, U43.pin20, U44.pin20, U45.pin14, U46.pin14, U47.pin20, U48.pin20, U49.pin20, U50.pin20, U51.pin20, U52.pin20, U53.pin14, U54.pin14, U55.pin14, U56.pin28, U57.pin20, U58.pin20, U59.pin20, U60.pin20, U61.pin20, U62.pin20, U63.pin16, U64.pin16, U65.pin20, U66.pin16, U67.pin16, U68.pin16, U69.pin16, U70.pin20, U71.pin20, U72.pin20, U76.pin20, U77.pin20, U78.pin20, U79.pin20, U80.pin14, U81.pin14, U82.pin14, U83.pin20

notes:
  5V DC
